# Fritzing sketch FSK_Circuit-With sensor (saved by Fritzing 0.8.7b)
breadboards: 1

parts:
  Part1 = Arduino Uno (Rev3)
  R1 = Resistor [tolerance=±5% resistance=10k package=THT]
  R2 = Resistor [tolerance=±5% resistance=2.2k package=THT]
  C1 = Ceramic Capacitor [capacitance=100nF package="0805 [SMD, multilayer]"]
  C2 = Ceramic Capacitor [capacitance=100nF package="0603 [SMD, multilayer]"]
  TRRS1 = Audio Jack (TRRS) 3.5mm [part_number="LUMBERG JEITA RC-5325A" package="RC-5325A [SMD]"]
  R3 = Resistor [tolerance=±5% resistance=2.2k package=THT]
  PART1 = ML8511 UV Sensor Breakout [part_number=SEN-12705]

nets:
  N1: Part1.A0, PART1.OUT
  3V3: Part1.A1, Part1.3V3, PART1.EN, PART1.3.3V
  N2: Part1.A5/SCL, TRRS1.TIP, TRRS1.RING1
  N3: Part1.D6_PWM, R1.Pin_1
  GND: Part1.GND, R2.Pin_1, TRRS1.RING2, R3.Pin_1, PART1.GND
  N4: R1.Pin_0, R2.Pin_0, C1.0
  N5: C1.1, C2.1
  N6: C2.0, TRRS1.SLEEVE, R3.Pin_0

custom parts:
  ML8511 UV Sensor Breakout: Description: The ML8511 breakout is an easy to use ultraviolet light sensor. The MP8511 UV Sensor works by outputing an analog signal in relation to the amount of UV light it detects. This breakout can be very handy in creating devices that warn the user of sunburn or detect the UV index as it relates to weather conditions. This sensor breakout can detect 280-390nm light most effectively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
